# Fritzing sketch Схема (saved by Fritzing 0.9.3b)
breadboards: 1

parts:
  Часть1 = Arduino Pro Mini v13
  YwRobot_Power_Supply1 = YwRobot Breadboard Power Supply [part_number=545043]
  LED1 = LED - 5mm [color="Red (633nm)" package="5 mm [THT]"]
  R1 = Resistor [tolerance=±5% resistance=220 package=THT]
  부품3 = FC-28 Soil Hygrometer Module - Probe
  부품4 = FC-28 Soil Hygrometer Module
  Q1 = PNP-Transistor [package="TO92 [THT]"]
  WATER_PUMP1 = water pump/motor  # not connected

nets:
  N1: Часть1.D4, LED1.cathode
  N2: Часть1.D3_PWM, 부품4.AO
  N3: Часть1.D2, Q1.B
  N4: YwRobot_Power_Supply1.VCC#5, YwRobot_Power_Supply1.VCC#6, 부품4.VCC
  N5: YwRobot_Power_Supply1.VCC#9, YwRobot_Power_Supply1.VCC#10
  N6: YwRobot_Power_Supply1.GND#11, YwRobot_Power_Supply1.GND#12, 부품4.GND, Q1.C
  N7: YwRobot_Power_Supply1.GND#13, YwRobot_Power_Supply1.GND#14, R1.Pin_1
  N8: LED1.anode, R1.Pin_0
  N9: 부품3.POS, 부품4.POS
  N10: 부품3.NEG, 부품4.NEG

custom parts:
  YwRobot Breadboard Power Supply: The YwRobot Breadboard Power Supply (MB-V2) has two power rails; they can be 5V or 3V3. Power to the module can be provided through the female USB socket or through the A10 (female) 2.1mm power jack.
  FC-28 Soil Hygrometer Module - Probe: The FC-28 is a soil hygrometer module that uses the Texas Instruments LM393 comparator chip to provide an analog measurement of soil humidity.
  FC-28 Soil Hygrometer Module: The FC-28 is a soil hygrometer module that uses the Texas Instruments LM393 comparator chip to provide an analog measurement of soil humidity. The digital output is high when soil moisture is over a certain threshold, as determined by adjusting the potentiometer.
  water pump/motor: WATER PUMP BY ARDUBLOCKTR
